# Fritzing sketch esp8266 htu21d (saved by Fritzing 0.9.2b)

parts:
  ESP8266 = NodeMCU V1.0
  HTU21D = Humidity Temperature Sensor SHT15

nets:
  N1: ESP8266.D1, HTU21D.SCL
  N2: ESP8266.D2, HTU21D.SDA
  3V3: ESP8266.3V3, HTU21D.VCC
  GND: ESP8266.GND, HTU21D.GND

custom parts:
  NodeMCU V1.0: ESP8266 based NodeMCU
  Humidity Temperature Sensor SHT15: Description: This is a simple breakout board for the SHT15 humidity sensor from Sensirion. The SHT15 digital humidity and temperature sensor is fully calibrated and offers high precision and excellent long-term stability at low cost. The digital CMOSens Technology integrates two sensors and readout circuitry on one single chip. These sensors are really impressive! Very sensitive and straight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
